// Logisim project TRABALHO.circ as structural Verilog: 1 circuit, main circuit main
module main (
  input  [1:0] SELEC,
  input  RESET
);

  wire CLK_out;
  wire [3:0] CONTADOR_q, LIMA_data, multiplexer_1_out, ROSA_data, SALERNO_data, VICENTE_data;
  wire [6:0] LETRAS_data, R0_q, R1_q, R2_q, R3_q, R4_q;

  Counter #(.max('h9), .width(4)) CONTADOR (
    .clr(RESET), .clk(CLK_out), .Q(CONTADOR_q));  // open: load, up, count, D, carry
  ROM #(.addrWidth(4), .dataWidth(4)) ROSA (.addr(CONTADOR_q), .data(ROSA_data));
  ROM #(.addrWidth(4), .dataWidth(4)) LIMA (.addr(CONTADOR_q), .data(LIMA_data));
  ROM #(.addrWidth(4), .dataWidth(4)) VICENTE (.addr(CONTADOR_q), .data(VICENTE_data));
  ROM #(.addrWidth(4), .dataWidth(4)) SALERNO (.addr(CONTADOR_q), .data(SALERNO_data));
  Multiplexer #(.enable("false"), .select(2), .width(4)) multiplexer_1 (
    .in0(ROSA_data), .in1(LIMA_data), .in2(VICENTE_data), .in3(SALERNO_data), .out(multiplexer_1_out));  // open: sel
  ROM #(.addrWidth(4), .dataWidth(7)) LETRAS (.addr(multiplexer_1_out), .data(LETRAS_data));
  _7_Segment_Display #(.decimalPoint("false")) u_7_segment_display_1 (
    .g(R4_q[6]), .f(R4_q[5]), .a(R4_q[0]), .b(R4_q[1]), .e(R4_q[4]), .d(R4_q[3]), .c(R4_q[2]));
  Register #(.width(7)) R0 (.D(LETRAS_data), .en(CLK_out), .clk(CLK_out), .Q(R0_q), .clr(RESET));
  _7_Segment_Display #(.decimalPoint("false")) u_7_segment_display_2 (
    .g(R3_q[6]), .f(R3_q[5]), .a(R3_q[0]), .b(R3_q[1]), .e(R3_q[4]), .d(R3_q[3]), .c(R3_q[2]));
  Register #(.width(7)) R1 (.D(R0_q), .en(CLK_out), .clk(CLK_out), .Q(R1_q), .clr(RESET));
  _7_Segment_Display #(.decimalPoint("false")) u_7_segment_display_3 (
    .g(R2_q[6]), .f(R2_q[5]), .a(R2_q[0]), .b(R2_q[1]), .e(R2_q[4]), .d(R2_q[3]), .c(R2_q[2]));
  Register #(.width(7)) R2 (.D(R1_q), .en(CLK_out), .clk(CLK_out), .Q(R2_q), .clr(RESET));
  Clock CLK (.out(CLK_out));
  _7_Segment_Display #(.decimalPoint("false")) u_7_segment_display_4 (
    .g(R1_q[6]), .f(R1_q[5]), .a(R1_q[0]), .b(R1_q[1]), .e(R1_q[4]), .d(R1_q[3]), .c(R1_q[2]));
  Register #(.width(7)) R3 (.D(R2_q), .en(CLK_out), .clk(CLK_out), .Q(R3_q), .clr(RESET));
  Register #(.width(7)) R4 (.D(R3_q), .en(CLK_out), .clk(CLK_out), .Q(R4_q), .clr(RESET));

  // Notes on the sheet:
  //   contents of ROSA (hex, n*v repeats v):
  //   0 0 0 8 7 9 1
  //   contents of LIMA (hex, n*v repeats v):
  //   0 0 0 4 3 5 1
  //   contents of VICENTE (hex, n*v repeats v):
  //   0 0 0 a 3 b 2 6 c 2
  //   contents of SALERNO (hex, n*v repeats v):
  //   0 0 0 9 1 4 2 8 6 7
  //   contents of LETRAS (hex, n*v repeats v):
  //   0 77 79 6 38 4f 43 3f 57 6d 3e 39 7 73
endmodule
